# Fritzing sketch Arduino_eine_Batterie (saved by Fritzing 0.9.2b)

parts:
  J1 = Basic Servo
  Bauteil1 = Arduino Uno (Rev3)

nets:
  GND: J1.gnd, Bauteil1.GND
  VCC: J1.vcc, Bauteil1.5V
  N1: J1.pulse, Bauteil1.D9_PWM
