# Fritzing sketch Arduino_zwei_Batterien (saved by Fritzing 0.9.2b)

parts:
  J1 = Basic Servo
  Bauteil1 = Arduino Uno (Rev3)
  VCC1 = Battery block 9V

nets:
  GND: J1.gnd, Bauteil1.GND, VCC1.-
  N1: J1.vcc, VCC1.+
  N2: J1.pulse, Bauteil1.D9_PWM
