# Fritzing sketch RaspberryPi_eine_Batterie (saved by Fritzing 0.9.2b)

parts:
  Raspberry_Pi1 = Raspberry Pi B rev2
  J1 = Basic Servo

nets:
  5V: Raspberry_Pi1.5V, J1.vcc
  GND: Raspberry_Pi1.GND, J1.gnd
  N1: Raspberry_Pi1.GPIO_11, J1.pulse
