# Fritzing sketch RaspberryPi_zwei_Batterien (saved by Fritzing 0.9.2b)

parts:
  Raspberry_Pi1 = Raspberry Pi B rev2
  J1 = Basic Servo
  VCC1 = Battery block 9V

nets:
  GND: Raspberry_Pi1.GND, J1.gnd, VCC1.-
  N1: Raspberry_Pi1.GPIO_11, J1.pulse
